# Fritzing sketch led_to_bag (saved by Fritzing 0.9.3b)
breadboards: 1

parts:
  Componente1 = Arduino Uno (Rev3)
  R2 = Resistor [tolerance=±5% resistance=220 package=THT]
  R4 = Resistor [tolerance=±5% resistance=220 package=THT]
  R5 = Resistor [tolerance=±5% resistance=10k package=THT]
  R6 = Resistor [tolerance=±5% resistance=10k package=THT]
  R7 = Resistor [tolerance=±5% resistance=220 package=THT]
  R3 = Resistor [tolerance=±5% resistance=220 package=THT]
  R8 = Rotary Potentiometer (Small) [maximum_resistance=100kΩ package=THT]
  S1 = Pushbutton [package="[THT]"]
  S2 = Pushbutton [package="[THT]"]
  LED1 = smd LED [color="Green (565nm)" package="1206 [SMD]"]
  LED2 = smd LED [color="Green (565nm)" package="1206 [SMD]"]
  LED3 = smd LED [color="Green (565nm)" package="1206 [SMD]"]
  LED4 = smd LED [color="Red (660nm)" package="1206 [SMD]"]
  LED5 = smd LED [color="White (8000K)" package="1206 [SMD]"]

nets:
  N1: Componente1.A5/SCL, R8.wiper
  N2: Componente1.D9_PWM, LED5.anode
  N3: Componente1.D10_PWM/SS, LED3.anode
  N4: Componente1.D13/SCK, LED4.anode
  N5: Componente1.D2, Componente1.D3_PWM, R8.leg2, S1.Pin_1, S1.Pin_2, S2.Pin_1, S2.Pin_2
  N6: Componente1.D5_PWM, LED1.anode
  N7: Componente1.D6_PWM, LED2.anode
  N8: R2.Pin_0, LED2.cathode
  N9: R2.Pin_1, R4.Pin_1, R5.Pin_1, R6.Pin_1, R7.Pin_1, R3.Pin_1, R8.leg1, LED4.cathode
  N10: R4.Pin_0, LED1.cathode
  N11: R5.Pin_0, S2.Pin_3, S2.Pin_4
  N12: R6.Pin_0, S1.Pin_3, S1.Pin_4
  N13: R7.Pin_0, LED3.cathode
  N14: R3.Pin_0, LED5.cathode
