# Fritzing sketch iot (saved by Fritzing 0.9.4)
breadboards: 2

parts:
  Componente1 = Arduino Uno (Rev3)
  J1 = Basic Servo
  Componente2 = Bluetooth HC-05 Macho
  LED9 = smd LED [color="Red (633nm)" package="0805 [SMD]"]
  R8 = Resistor [tolerance=±5% resistance=220 package=THT]
  LED11 = smd LED [color="Red (633nm)" package="0805 [SMD]"]
  R10 = Resistor [tolerance=±5% resistance=220 package=THT]
  LED12 = smd LED [color="Red (633nm)" package="0805 [SMD]"]
  R11 = Resistor [tolerance=±5% resistance=220 package=THT]
  LED13 = smd LED [color="Red (633nm)" package="0805 [SMD]"]
  R12 = Resistor [tolerance=±5% resistance=220 package=THT]
  LED14 = smd LED [color="Red (633nm)" package="0805 [SMD]"]
  R13 = Resistor [tolerance=±5% resistance=220 package=THT]
  WeMos_D1_Mini1 = WeMos D1 Mini
  U1 = POT [package=pot_alpha_rv16af-20]

nets:
  N1: Componente1.D8, LED14.anode
  N2: Componente1.D9_PWM, LED13.anode
  N3: Componente1.D10_PWM/SS, LED12.anode
  GND: Componente1.GND, J1.gnd, Componente2.GND, R11.Pin_0, R12.Pin_0, R13.Pin_0
  N4: Componente1.D2, Componente2.TXD
  N5: Componente1.D3_PWM, Componente2.RXD
  N6: Componente1.D6_PWM, J1.pulse
  VCC: Componente1.5V, J1.vcc, Componente2.VCC
  N7: LED9.cathode, R8.Pin_1
  N8: LED9.anode, WeMos_D1_Mini1.D1
  N9: R8.Pin_0, R10.Pin_0, WeMos_D1_Mini1.G, U1.E
  N10: LED11.cathode, R10.Pin_1
  N11: LED11.anode, WeMos_D1_Mini1.D2
  N12: LED12.cathode, R11.Pin_1
  N13: LED13.cathode, R12.Pin_1
  N14: LED14.cathode, R13.Pin_1
  N15: WeMos_D1_Mini1.3V3, U1.A
  N16: WeMos_D1_Mini1.A0, U1.S
